# Fritzing sketch pixar (saved by Fritzing 0.9.3b)
breadboards: 1

parts:
  Componente1 = Arduino Mega 2560 (Rev3)
  WeMos_D1_Mini_Relay_Shield_V1 = WeMos D1 Mini Relay Shield
  IR1 = TSOP312.., 314.. [package=THT]
  BAT1 = BC9VPC [package=bc9vpc]
  LED1 = LED - 5mm [color="Red (633nm)" package="5 mm [THT]"]

nets:
  N1: Componente1.D12_PWM, WeMos_D1_Mini_Relay_Shield_V1.D1
  N2: Componente1.D8_PWM, IR1.GND
  5V: Componente1.5V, WeMos_D1_Mini_Relay_Shield_V1.5V, IR1.Data
  N3: Componente1.GND, WeMos_D1_Mini_Relay_Shield_V1.G, IR1.Vs
  N4: BAT1.V-, LED1.cathode

notes:
  Carregador de Smartphone -
  entrada - bivolt - saida 4,75v- 0,55A
  Led representa uma luminaria com varios leds em serie
  Modulo rele

// code stored in the sketch: pixar.ino

#include <boarddefs.h>


#include <IRremote.h>

#include <IRremoteInt.h>

#include <ir_Lego_PF_BitStreamEncoder.h>



//alterar nome

int porta_rele = 12;

int rec = 8;

IRrecv irrecv(rec);



decode_results results;

  

void setup(){

  pinMode(porta_rele, OUTPUT); 

  Serial.begin(9600);

  Serial.println("Enabling IRin");

  irrecv.enableIRIn();

  Serial.println("Enabled IRin");

}

   

void loop()

{ 

  if (irrecv.decode(&results)) {

    Serial.println(results.value, DEC);

    irrecv.resume(); // Receive the next value

  }

  

  delay(100);

  

  if(results.value == 4129172055){

    digitalWrite(porta_rele,HIGH);

    }

  if(results.value == 1849971288){

    digitalWrite(porta_rele,LOW);

    }

 

  delay(2000);

  

}
